// Logisim project Multiplexers.circ as structural Verilog: 36 circuits, main circuit TwoToOne
module TwoToOne (
  input  in0,
  input  s,
  input  in1,
  output z
);

  wire nand_1_out, nand_2_out, not_1_out;

  not not_1 (not_1_out, s);
  nand nand_1 (nand_1_out, in0, not_1_out);
  nand nand_2 (nand_2_out, in1, s);
  nand nand_3 (z, nand_1_out, nand_2_out);

  // Notes on the sheet:
  //   14 transistors
  //   2 to 1 Mux
  //   George Yue
  //   max(s+2.75,in0+2,in1+2)
  //   max 
endmodule

module FourToOne (
  input  in0,
  input  in1,
  input  in2,
  input  in3,
  input  s1,
  input  s0,
  output z
);

  wire twotoone_1_z, twotoone_2_z;

  TwoToOne twotoone_1 (.in0(in0), .s(s0), .in1(in1), .z(twotoone_1_z));
  TwoToOne twotoone_2 (.in0(in2), .s(s0), .in1(in3), .z(twotoone_2_z));
  TwoToOne twotoone_3 (.in0(twotoone_1_z), .s(s1), .in1(twotoone_2_z), .z(z));

  // Notes on the sheet:
  //   42 transistors
  //   max(s0+4.75,s1+2.75,in0+4,in1+4,in2+4,in3+4)
  //   4 to 1 Mux
  //   George Yue
endmodule

module mx2i (
  input  in0,
  input  in1,
  input  s,
  output z
);

  wire not_1_out, transmission_1_p4;

  not not_1 (not_1_out, s);
  // Transmission_Gate transmission_1: pin names not known; wires that end beside it: in0, s, not_1_out, transmission_1_p4
  // Transmission_Gate transmission_2: pin names not known; wires that end beside it: in1, not_1_out, s, transmission_1_p4
  not not_2 (z, transmission_1_p4);

  // Notes on the sheet:
  //   8 transistors
  //   max(s+1.75,in0+1,in1+1)
  //   mx2i
  //   George Yue
endmodule

module mx4i (
  input  in0,
  input  in1,
  input  in2,
  input  s1,
  input  in3,
  input  s0,
  output z
);

  wire mx2i_1_z, mx2i_2_z;

  mx2i mx2i_1 (.in0(in0), .in1(in1), .s(s0), .z(mx2i_1_z));
  mx2i mx2i_2 (.in0(in2), .in1(in3), .s(s0), .z(mx2i_2_z));
  mx2i mx2i_3 (.in0(mx2i_1_z), .in1(mx2i_2_z), .s(s1), .z(z));

  // Notes on the sheet:
  //   24 transistors
  //   mx4i
  //   George Yue
  //   max(s0+2.75,s1+1.75,in0+2,in1+2,in2+2,in3+2)
endmodule

module EightBitCSA (
  input  in_1,
  input  [7:0] in_2,
  input  [7:0] in_3,
  output [7:0] _10_5,
  output cout
);

  wire fourbitadder0_1_cout, fourbitadder0_2_cout, fourbitadder1_1_cout, mx2i_1_z;
  wire [3:0] fourbitadder0_1_s, fourbitadder1_1_s, mx2i_4_1_cout;

  mx2i mx2i_1 (.in0(fourbitadder0_1_cout), .in1(fourbitadder1_1_cout), .s(fourbitadder0_2_cout), .z(mx2i_1_z));
  FourBitAdder1 fourbitadder1_1 (.a(in_2[7:4]), .b(in_3[7:4]), .s(fourbitadder1_1_s), .cout(fourbitadder1_1_cout));
  mx2i_4 mx2i_4_1 (.in1(fourbitadder1_1_s), .in0(fourbitadder0_1_s), .s(fourbitadder0_2_cout), .cout(mx2i_4_1_cout));
  FourBitAdder0 fourbitadder0_1 (
    .a(in_2[7:4]), .b(in_3[7:4]), .s(fourbitadder0_1_s), .cout(fourbitadder0_1_cout));  // open: in_1
  not not_1 (cout, mx2i_1_z);
  assign _10_5[7:4] = ~mx2i_4_1_cout;  // NOT_Gate not_2, 4 bits wide
  FourBitAdder0 fourbitadder0_2 (
    .a(in_2[3:0]), .b(in_3[3:0]), .in_1(in_1), .s(_10_5[3:0]), .cout(fourbitadder0_2_cout));

  // Notes on the sheet:
  //   8
  //   9.75
  //   8.75
  //   8
  //   9.75
  //   8.75
  //   8
  //   8.75
  //   10.5
endmodule

module FA0 (
  input  a,
  input  b,
  output Sum,
  output Cout
);

  wire nor_1_out;

  and and_1 (Cout, a, b);
  nor nor_1 (nor_1_out, a, b);
  nor nor_2 (Sum, nor_1_out, Cout);

  // Notes on the sheet:
  //   0
  //   0
  //   14 transistors
  //   2.75
  //   1.75
  //   FA0
  //   George Yue
endmodule

module FA1 (
  input  a,
  input  b,
  output Sum,
  output Cout
);

  wire nand_1_out;

  or or_1 (Cout, a, b);
  nand nand_1 (nand_1_out, a, b);
  nand nand_2 (Sum, nand_1_out, Cout);

  // Notes on the sheet:
  //   0
  //   14 transistors
  //   2.75
  //   1.75
  //   FA1
  //   George Yue
endmodule

module FAopt1 (
  input  a,
  input  b,
  input  Cin,
  output Sum,
  output Cout
);

  wire nand_1_out, nand_2_out, nor_1_out, nor_2_out, nor_3_out, not_1_out, not_2_out;

  nand nand_1 (nand_1_out, a, b);
  nor nor_1 (nor_1_out, a, b);
  not not_1 (not_1_out, nand_1_out);
  nor nor_2 (nor_2_out, nor_1_out, not_1_out);
  nor nor_3 (nor_3_out, nor_2_out, Cin);
  nand nand_2 (nand_2_out, nor_2_out, Cin);
  not not_2 (not_2_out, nand_2_out);
  nor nor_4 (Sum, nor_3_out, not_2_out);
  nand nand_3 (Cout, nand_2_out, nand_1_out);

  // Notes on the sheet:
  //   0
  //   0
  //   32 transistors
  //   If cin < 2.75    5.5
  //   If cin > 2.75    Cin + 2.75
  //   If cin < 2.75  4.75
  //   If Cin > 2.75   Cin + 2
  //   FAopt1
  //   George Yue
endmodule

module FAopt2 (
  input  a,
  input  b,
  input  Cin,
  output Sum,
  output Cout
);

  wire nand_1_out, nand_2_out, nand_3_out, nand_4_out, nor_1_out, nor_2_out, nor_3_out, not_1_out, not_2_out;

  nand nand_1 (nand_1_out, a, b);
  nor nor_1 (nor_1_out, a, b);
  not not_1 (not_1_out, nand_1_out);
  nor nor_2 (nor_2_out, nor_1_out, not_1_out);
  nor nor_3 (nor_3_out, nor_2_out, Cin);
  nand nand_2 (nand_2_out, nor_2_out, Cin);
  nand nand_3 (nand_3_out, b, Cin);
  nand nand_4 (nand_4_out, a, Cin);
  not not_2 (not_2_out, nand_2_out);
  nor nor_4 (Sum, nor_3_out, not_2_out);
  nand nand_5 (Cout, nand_1_out, nand_3_out, nand_4_out);

  // Notes on the sheet:
  //   0
  //   0
  //   42 transistors
  //   If cin < 2.75    5.5
  //   If cin > 2.75    Cin + 2.75
  //   Cin + 2.25
  //   FAopt1
  //   George Yue
endmodule

module FourBitAdder0 (
  input  in_1,
  input  [3:0] a,
  input  [3:0] b,
  output [3:0] s,
  output cout
);

  wire faopt1_2_cout, faopt1_3_cout, faopt2_1_cout;

  FAopt1 faopt1_1 (.a(a[3]), .b(b[3]), .Cin(faopt1_2_cout), .Sum(s[3]), .Cout(cout));
  FAopt1 faopt1_2 (.a(a[2]), .b(b[2]), .Cin(faopt2_1_cout), .Sum(s[2]), .Cout(faopt1_2_cout));
  FAopt2 faopt2_1 (.a(a[1]), .b(b[1]), .Cin(faopt1_3_cout), .Sum(s[1]), .Cout(faopt2_1_cout));
  FAopt1 faopt1_3 (.a(a[0]), .b(b[0]), .Cin(in_1), .Sum(s[0]), .Cout(faopt1_3_cout));

  // Notes on the sheet:
  //   8.75
  //   9.5
  //   6.75
  //   4.75
  //   7.5
  //   5.5
  //   9.5
  //   8.75
  //   1.75
  //   2.75
endmodule

module FourBitAdder1 (
  input  [3:0] a,
  input  [3:0] b,
  output [3:0] s,
  output cout
);

  wire fa1_1_cout, faopt1_2_cout, faopt2_1_cout;

  FAopt1 faopt1_1 (.a(a[3]), .b(b[3]), .Cin(faopt1_2_cout), .Sum(s[3]), .Cout(cout));
  FAopt1 faopt1_2 (.a(a[2]), .b(b[2]), .Cin(faopt2_1_cout), .Sum(s[2]), .Cout(faopt1_2_cout));
  FAopt2 faopt2_1 (.a(a[1]), .b(b[1]), .Cin(fa1_1_cout), .Sum(s[1]), .Cout(faopt2_1_cout));
  FA1 fa1_1 (.a(a[0]), .b(b[0]), .Sum(s[0]), .Cout(fa1_1_cout));

  // Notes on the sheet:
  //   8.75
  //   9.5
  //   6.75
  //   4.75
  //   7.5
  //   5.5
  //   9.5
  //   8.75
  //   1.75
  //   2.75
endmodule

module mx2i_4 (
  input  [3:0] in0,
  input  [3:0] in1,
  input  s,
  output [3:0] cout
);

  mx2i mx2i_1 (.in0(in0[0]), .in1(in1[0]), .s(s), .z(cout[0]));
  mx2i mx2i_2 (.in0(in0[1]), .in1(in1[1]), .s(s), .z(cout[1]));
  mx2i mx2i_3 (.in0(in0[2]), .in1(in1[2]), .s(s), .z(cout[2]));
  mx2i mx2i_4 (.in0(in0[3]), .in1(in1[3]), .s(s), .z(cout[3]));
endmodule

module SixteenBitCSA (
  input  in_1,
  input  [15:0] in_2,
  input  [15:0] in_3,
  output [15:0] out_4,
  output cout
);

  wire eightbitcsa1_1_cout, eightbitcsa_1_cout, eightbitcsa_2_cout, mx2i_1_z;
  wire [7:0] eightbitcsa1_1_out_3, eightbitcsa_1__10_5, mx2i_8_1_out_4;

  mx2i mx2i_1 (.in0(eightbitcsa_1_cout), .in1(eightbitcsa1_1_cout), .s(eightbitcsa_2_cout), .z(mx2i_1_z));
  EightBitCSA1 eightbitcsa1_1 (
    .in_1(in_2[15:8]), .in_2(in_3[15:8]), .out_3(eightbitcsa1_1_out_3), .cout(eightbitcsa1_1_cout));
  mx2i_8 mx2i_8_1 (
    .in1(eightbitcsa1_1_out_3), .s(eightbitcsa_2_cout), .in0(eightbitcsa_1__10_5), .out_4(mx2i_8_1_out_4));
  EightBitCSA eightbitcsa_1 (
    .in_2(in_2[15:8]), .in_3(in_3[15:8]), ._10_5(eightbitcsa_1__10_5), .cout(eightbitcsa_1_cout));  // open: in_1
  not not_1 (cout, mx2i_1_z);
  assign out_4[15:8] = ~mx2i_8_1_out_4;  // NOT_Gate not_2, 8 bits wide
  EightBitCSA eightbitcsa_2 (
    .in_2(in_2[7:0]), .in_3(in_3[7:0]), .in_1(in_1), ._10_5(out_4[7:0]), .cout(eightbitcsa_2_cout));

  // Notes on the sheet:
  //   10.5
  //   12.25
  //   10.5
  //   10.5
  //   12.25
  //   10.5
  //   10.5
  //   10.5
  //   13
  //   13
endmodule

module mx2i_8 (
  input  [7:0] in0,
  input  [7:0] in1,
  input  s,
  output [7:0] out_4
);

  mx2i mx2i_1 (.in0(in0[0]), .in1(in1[0]), .s(s), .z(out_4[0]));
  mx2i mx2i_2 (.in0(in0[1]), .in1(in1[1]), .s(s), .z(out_4[1]));
  mx2i mx2i_3 (.in0(in0[2]), .in1(in1[2]), .s(s), .z(out_4[2]));
  mx2i mx2i_4 (.in0(in0[3]), .in1(in1[3]), .s(s), .z(out_4[3]));
  mx2i mx2i_5 (.in0(in0[4]), .in1(in1[4]), .s(s), .z(out_4[4]));
  mx2i mx2i_6 (.in0(in0[5]), .in1(in1[5]), .s(s), .z(out_4[5]));
  mx2i mx2i_7 (.in0(in0[6]), .in1(in1[6]), .s(s), .z(out_4[6]));
  mx2i mx2i_8 (.in0(in0[7]), .in1(in1[7]), .s(s), .z(out_4[7]));
endmodule

module EightBitCSA1 (
  input  [7:0] in_1,
  input  [7:0] in_2,
  output [7:0] out_3,
  output cout
);

  wire fourbitadder0_1_cout, fourbitadder1_1_cout, fourbitadder1_2_cout, mx2i_1_z;
  wire [3:0] fourbitadder0_1_s, fourbitadder1_1_s, mx2i_4_1_cout;

  mx2i mx2i_1 (.in0(fourbitadder0_1_cout), .in1(fourbitadder1_1_cout), .s(fourbitadder1_2_cout), .z(mx2i_1_z));
  FourBitAdder1 fourbitadder1_1 (.a(in_1[7:4]), .b(in_2[7:4]), .s(fourbitadder1_1_s), .cout(fourbitadder1_1_cout));
  mx2i_4 mx2i_4_1 (.in1(fourbitadder1_1_s), .in0(fourbitadder0_1_s), .s(fourbitadder1_2_cout), .cout(mx2i_4_1_cout));
  FourBitAdder0 fourbitadder0_1 (
    .a(in_1[7:4]), .b(in_2[7:4]), .s(fourbitadder0_1_s), .cout(fourbitadder0_1_cout));  // open: in_1
  not not_1 (cout, mx2i_1_z);
  assign out_3[7:4] = ~mx2i_4_1_cout;  // NOT_Gate not_2, 4 bits wide
  FourBitAdder1 fourbitadder1_2 (.a(in_1[3:0]), .b(in_2[3:0]), .s(out_3[3:0]), .cout(fourbitadder1_2_cout));
endmodule

module SixteenBitAS (
  input  OP,
  input  [15:0] B,
  input  [15:0] A,
  output [15:0] out_4,
  output overflow
);

  wire not_2_out, xor_1_out, xor_2_out;
  wire [15:0] multiplexer_1_out, not_1_out;

  assign not_1_out = ~B;  // NOT_Gate not_1, 16 bits wide
  Multiplexer #(.width(16)) multiplexer_1 (.in0(B), .in1(not_1_out), .out(multiplexer_1_out), .sel(OP));
  Adder #(.width(16)) adder_1 (.a(multiplexer_1_out), .b(A), .out(out_4), .cin(OP));  // open: cout
  xor xor_1 (xor_1_out, out_4[15], multiplexer_1_out[15]);
  xor xor_2 (xor_2_out, multiplexer_1_out[15], A[15]);
  not not_2 (not_2_out, xor_2_out);
  and and_1 (overflow, xor_1_out, not_2_out);
endmodule

module SixteenBitAS2 (
  input  OP,
  input  [15:0] B,
  input  [15:0] A,
  output [15:0] sum,
  output overflow
);

  wire not_2_out, xor_1_out, xor_2_out;
  wire [15:0] multiplexer_1_out, not_1_out;

  assign not_1_out = ~B;  // NOT_Gate not_1, 16 bits wide
  Multiplexer #(.width(16)) multiplexer_1 (.in0(B), .in1(not_1_out), .out(multiplexer_1_out), .sel(OP));
  SixteenBitCSA sixteenbitcsa_1 (.in_2(multiplexer_1_out), .in_3(A), .in_1(OP), .out_4(sum));  // open: cout
  xor xor_1 (xor_1_out, sum[15], multiplexer_1_out[15]);
  xor xor_2 (xor_2_out, multiplexer_1_out[15], A[15]);
  not not_2 (not_2_out, xor_2_out);
  and and_1 (overflow, xor_1_out, not_2_out);
endmodule

module cir1 (
  input  A,
  input  B,
  input  OP,
  input  R,
  output overflow
);

  wire multiplexer_1_out, not_1_out, not_2_out, xor_1_out, xor_2_out;

  not not_1 (not_1_out, B);
  Multiplexer multiplexer_1 (.in0(B), .in1(not_1_out), .out(multiplexer_1_out), .sel(OP));
  xor xor_1 (xor_1_out, A, multiplexer_1_out);
  xor xor_2 (xor_2_out, A, R);
  not not_2 (not_2_out, xor_1_out);
  and and_1 (overflow, not_2_out, xor_2_out);
endmodule

module r0r1 (
  input  rst,
  input  subtract,
  input  [15:0] in_3
);

  wire clk;
  wire [15:0] R0, R1, sixteenbitas2_1_sum;

  Clock u_clk (.out(clk));
  SixteenBitAS2 sixteenbitas2_1 (.OP(subtract), .B(R1), .A(R0), .sum(sixteenbitas2_1_sum));  // open: overflow
  Hex_Digit_Display hex_digit_display_1 (.value(R0[15:12]));  // open: dp
  Hex_Digit_Display hex_digit_display_2 (.value(R0[11:8]));  // open: dp
  Hex_Digit_Display hex_digit_display_3 (.value(R0[7:4]));  // open: dp
  Hex_Digit_Display hex_digit_display_4 (.value(R0[3:0]));  // open: dp
  Register #(.width(16)) u_R0 (.D(sixteenbitas2_1_sum), .en(1'b1), .clk(clk), .Q(R0), .clr(rst));
  Register #(.width(16)) u_R1 (.D(in_3), .en(1'b1), .clk(clk), .Q(R1), .clr(rst));
endmodule

module regWE (
  input  [1:0] Rd,
  input  regWrite,
  output reg0WE,
  output reg1WE,
  output reg2WE,
  output reg3WE
);

  wire not_1_out, not_2_out;
  wire [1:0] multiplexer_1_out;

  Multiplexer #(.width(2)) multiplexer_1 (.in0(2'b00), .in1(Rd), .out(multiplexer_1_out), .sel(regWrite));
  not not_1 (not_1_out, regWrite);
  not not_2 (not_2_out, multiplexer_1_out[1]);
  Multiplexer multiplexer_2 (.in0(multiplexer_1_out[1]), .in1(1'b0), .out(reg2WE), .sel(multiplexer_1_out[0]));
  Multiplexer multiplexer_3 (.in0(1'b0), .in1(multiplexer_1_out[1]), .out(reg3WE), .sel(multiplexer_1_out[0]));
  nor nor_1 (reg0WE, multiplexer_1_out[0], multiplexer_1_out[1], not_1_out);
  and and_1 (reg1WE, multiplexer_1_out[0], not_2_out);
endmodule

module scrSel (
  input  [1:0] sel,
  input  [15:0] reg0,
  input  [15:0] reg1,
  input  [15:0] reg2,
  input  [15:0] reg3,
  output [15:0] regOut
);

  Multiplexer #(.select(2), .width(16)) multiplexer_1 (
    .in0(reg0), .in1(reg1), .in2(reg2), .in3(reg3), .out(regOut), .sel(sel));
endmodule

module TestRegisters (
  input  rst,
  input  [1:0] Rd,
  input  [1:0] Rs,
  input  subtract
);

  wire clk, ovrfl, register_1_q, regwe_1_reg0we, regwe_1_reg1we, regwe_1_reg2we, regwe_1_reg3we;
  wire [15:0] A, B, R0, R1, R2, R3, sixteenbitas2_1_sum;

  Clock u_clk (.out(clk));
  Register #(.width(1)) register_1 (.D(1'b1), .en(ovrfl), .clk(clk), .Q(register_1_q), .clr(rst));
  Hex_Digit_Display hex_digit_display_1 (.value(R0[15:12]));  // open: dp
  Hex_Digit_Display hex_digit_display_2 (.value(R0[11:8]));  // open: dp
  SixteenBitAS2 sixteenbitas2_1 (.OP(subtract), .B(B), .A(A), .sum(sixteenbitas2_1_sum), .overflow(ovrfl));
  regWE regwe_1 (
    .Rd(Rd), .regWrite(1'b1), .reg0WE(regwe_1_reg0we), .reg1WE(regwe_1_reg1we), .reg2WE(regwe_1_reg2we),
    .reg3WE(regwe_1_reg3we));
  LED led_1 (.in(register_1_q));
  Hex_Digit_Display hex_digit_display_3 (.value(R0[7:4]));  // open: dp
  Hex_Digit_Display hex_digit_display_4 (.value(R0[3:0]));  // open: dp
  Hex_Digit_Display hex_digit_display_5 (.value(R1[15:12]));  // open: dp
  Hex_Digit_Display hex_digit_display_6 (.value(R1[11:8]));  // open: dp
  Hex_Digit_Display hex_digit_display_7 (.value(R1[7:4]));  // open: dp
  Hex_Digit_Display hex_digit_display_8 (.value(R1[3:0]));  // open: dp
  Register #(.width(16)) u_R0 (.D(sixteenbitas2_1_sum), .en(regwe_1_reg0we), .clk(clk), .Q(R0), .clr(rst));
  Register #(.width(16)) u_R1 (.D(sixteenbitas2_1_sum), .en(regwe_1_reg1we), .clk(clk), .Q(R1), .clr(rst));
  Register #(.width(16)) u_R2 (.D(sixteenbitas2_1_sum), .en(regwe_1_reg2we), .clk(clk), .Q(R2), .clr(rst));
  Register #(.width(16)) u_R3 (.D(sixteenbitas2_1_sum), .en(regwe_1_reg3we), .clk(clk), .Q(R3), .clr(rst));
  Hex_Digit_Display hex_digit_display_9 (.value(R2[15:12]));  // open: dp
  Hex_Digit_Display hex_digit_display_10 (.value(R2[11:8]));  // open: dp
  Hex_Digit_Display hex_digit_display_11 (.value(R2[7:4]));  // open: dp
  Hex_Digit_Display hex_digit_display_12 (.value(R2[3:0]));  // open: dp
  Hex_Digit_Display hex_digit_display_13 (.value(R3[15:12]));  // open: dp
  Hex_Digit_Display hex_digit_display_14 (.value(R3[11:8]));  // open: dp
  Hex_Digit_Display hex_digit_display_15 (.value(R3[7:4]));  // open: dp
  scrSel scrsel_1 (.sel(Rd), .reg0(R0), .reg1(R1), .reg2(R2), .reg3(R3), .regOut(A));
  scrSel scrsel_2 (.sel(Rs), .reg0(R0), .reg1(R1), .reg2(R2), .reg3(R3), .regOut(B));
  Hex_Digit_Display hex_digit_display_16 (.value(R3[3:0]));  // open: dp
endmodule

module FirstProgram (
  input  rst
);

  wire clk, not_1_out, not_2_out, op, ovrfl, register_1_q, regwe_1_reg0we, regwe_1_reg1we, regwe_1_reg2we,
       regwe_1_reg3we;
  wire [1:0] Rd, Rs;
  wire [3:0] ram_1_dout;
  wire [5:0] programcounter_1_pc;
  wire [15:0] A, B, R0, R1, R2, R3, sixteenbitas2_1_sum;

  Clock u_clk (.out(clk));
  Register #(.width(1)) register_1 (.D(1'b1), .en(ovrfl), .clk(clk), .Q(register_1_q), .clr(rst));
  Hex_Digit_Display hex_digit_display_1 (.value(R0[15:12]));  // open: dp
  Hex_Digit_Display hex_digit_display_2 (.value(R0[11:8]));  // open: dp
  LED led_1 (.in(register_1_q));
  SixteenBitAS2 sixteenbitas2_1 (.OP(op), .B(B), .A(A), .sum(sixteenbitas2_1_sum), .overflow(ovrfl));
  regWE regwe_1 (
    .Rd(Rd), .regWrite(1'b1), .reg0WE(regwe_1_reg0we), .reg1WE(regwe_1_reg1we), .reg2WE(regwe_1_reg2we),
    .reg3WE(regwe_1_reg3we));
  Hex_Digit_Display hex_digit_display_3 (.value(R0[7:4]));  // open: dp
  Hex_Digit_Display hex_digit_display_4 (.value(R0[3:0]));  // open: dp
  Hex_Digit_Display hex_digit_display_5 (.value(R1[15:12]));  // open: dp
  Hex_Digit_Display hex_digit_display_6 (.value(R1[11:8]));  // open: dp
  Hex_Digit_Display hex_digit_display_7 (.value(R1[7:4]));  // open: dp
  Hex_Digit_Display hex_digit_display_8 (.value(R1[3:0]));  // open: dp
  Register #(.width(16)) u_R0 (.D(sixteenbitas2_1_sum), .en(regwe_1_reg0we), .clk(clk), .Q(R0), .clr(rst));
  Register #(.width(16)) u_R1 (.D(sixteenbitas2_1_sum), .en(regwe_1_reg1we), .clk(clk), .Q(R1), .clr(rst));
  Register #(.width(16)) u_R2 (.D(sixteenbitas2_1_sum), .en(regwe_1_reg2we), .clk(clk), .Q(R2), .clr(rst));
  Register #(.width(16)) u_R3 (.D(sixteenbitas2_1_sum), .en(regwe_1_reg3we), .clk(clk), .Q(R3), .clr(rst));
  Hex_Digit_Display hex_digit_display_9 (.value(R2[15:12]));  // open: dp
  Hex_Digit_Display hex_digit_display_10 (.value(R2[11:8]));  // open: dp
  Hex_Digit_Display hex_digit_display_11 (.value(R2[7:4]));  // open: dp
  Hex_Digit_Display hex_digit_display_12 (.value(R2[3:0]));  // open: dp
  Hex_Digit_Display hex_digit_display_13 (.value(R3[15:12]));  // open: dp
  Hex_Digit_Display hex_digit_display_14 (.value(R3[11:8]));  // open: dp
  Hex_Digit_Display hex_digit_display_15 (.value(R3[7:4]));  // open: dp
  scrSel scrsel_1 (.sel(Rd), .reg0(R0), .reg1(R1), .reg2(R2), .reg3(R3), .regOut(A));
  scrSel scrsel_2 (.sel(Rs), .reg0(R0), .reg1(R1), .reg2(R2), .reg3(R3), .regOut(B));
  ProgramCounter programcounter_1 (.clk(clk), .rst(rst), .pc(programcounter_1_pc));
  Hex_Digit_Display hex_digit_display_16 (.value(R3[3:0]));  // open: dp
  RAM #(.addrWidth(6), .asyncread("true"), .trigger("falling")) ram_1 (
    .addr(programcounter_1_pc), .we(1'b0), .oe(1'b1), .clk(clk), .dout({Rd, Rs, ram_1_dout}));  // open: din
  not not_1 (not_1_out, ram_1_dout[3]);
  not not_2 (not_2_out, ram_1_dout[2]);
  and and_1 (op, not_1_out, not_2_out, ram_1_dout[1], ram_1_dout[0]);

  // Notes on the sheet:
  //   4c41 5341 7b43 537d
  //   b3 43 e2 32 82
endmodule

module ProgramCounter (
  input  clk,
  input  rst,
  output [5:0] pc
);

  wire [5:0] adder_1_out;

  Register #(.width(6)) R (.D(adder_1_out), .clk(clk), .Q(pc), .clr(rst));  // open: en
  Adder #(.width(6)) adder_1 (.a(6'b000001), .b(pc), .out(adder_1_out));  // open: cin, cout
endmodule

module FirstProgramAgain (
  input  rst
);

  wire clk, d_ff_1_q, d_ff_2_q, d_ff_3_q, d_ff_4_q, op, ovrfl, register_1_q, regwe_1_reg0we, regwe_1_reg1we,
       regwe_1_reg2we, regwe_1_reg3we;
  wire [1:0] Rd, Rs;
  wire [5:0] programcounter_1_pc;
  wire [7:0] InstructionRegister_q, ram_1_dout;
  wire [15:0] A, B, R0, R1, R2, R3, sixteenbitas2_1_sum;

  D_Flip_Flop d_ff_1 (.D(1'b1), .clk(clk), .Q(d_ff_1_q), .reset(rst));  // open: Qn, preset
  Clock u_clk (.out(clk));
  D_Flip_Flop d_ff_2 (.D(1'b1), .clk(clk), .Q(d_ff_2_q), .reset(rst));  // open: Qn, preset
  D_Flip_Flop d_ff_3 (.D(d_ff_1_q), .clk(clk), .Q(d_ff_3_q), .reset(rst));  // open: Qn, preset
  D_Flip_Flop d_ff_4 (.D(d_ff_2_q), .clk(clk), .Q(d_ff_4_q), .reset(rst));  // open: Qn, preset
  Register #(.width(1)) register_1 (.D(d_ff_4_q), .en(ovrfl), .clk(clk), .Q(register_1_q), .clr(rst));
  Hex_Digit_Display hex_digit_display_1 (.value(R0[15:12]));  // open: dp
  Hex_Digit_Display hex_digit_display_2 (.value(R0[11:8]));  // open: dp
  LED led_1 (.in(register_1_q));
  SixteenBitAS2 sixteenbitas2_1 (.OP(op), .B(B), .A(A), .sum(sixteenbitas2_1_sum), .overflow(ovrfl));
  regWE regwe_1 (
    .Rd(Rd), .regWrite(d_ff_3_q), .reg0WE(regwe_1_reg0we), .reg1WE(regwe_1_reg1we), .reg2WE(regwe_1_reg2we),
    .reg3WE(regwe_1_reg3we));
  Hex_Digit_Display hex_digit_display_3 (.value(R0[7:4]));  // open: dp
  Hex_Digit_Display hex_digit_display_4 (.value(R0[3:0]));  // open: dp
  Hex_Digit_Display hex_digit_display_5 (.value(R1[15:12]));  // open: dp
  Hex_Digit_Display hex_digit_display_6 (.value(R1[11:8]));  // open: dp
  Hex_Digit_Display hex_digit_display_7 (.value(R1[7:4]));  // open: dp
  Hex_Digit_Display hex_digit_display_8 (.value(R1[3:0]));  // open: dp
  Register #(.width(16)) u_R0 (.D(sixteenbitas2_1_sum), .en(regwe_1_reg0we), .clk(clk), .Q(R0), .clr(rst));
  Register #(.width(16)) u_R1 (.D(sixteenbitas2_1_sum), .en(regwe_1_reg1we), .clk(clk), .Q(R1), .clr(rst));
  Register #(.width(16)) u_R2 (.D(sixteenbitas2_1_sum), .en(regwe_1_reg2we), .clk(clk), .Q(R2), .clr(rst));
  Register #(.width(16)) u_R3 (.D(sixteenbitas2_1_sum), .en(regwe_1_reg3we), .clk(clk), .Q(R3), .clr(rst));
  Hex_Digit_Display hex_digit_display_9 (.value(R2[15:12]));  // open: dp
  Hex_Digit_Display hex_digit_display_10 (.value(R2[11:8]));  // open: dp
  Hex_Digit_Display hex_digit_display_11 (.value(R2[7:4]));  // open: dp
  Hex_Digit_Display hex_digit_display_12 (.value(R2[3:0]));  // open: dp
  Hex_Digit_Display hex_digit_display_13 (.value(R3[15:12]));  // open: dp
  Hex_Digit_Display hex_digit_display_14 (.value(R3[11:8]));  // open: dp
  Hex_Digit_Display hex_digit_display_15 (.value(R3[7:4]));  // open: dp
  scrSel scrsel_1 (.sel(Rd), .reg0(R0), .reg1(R1), .reg2(R2), .reg3(R3), .regOut(A));
  scrSel scrsel_2 (.sel(Rs), .reg0(R0), .reg1(R1), .reg2(R2), .reg3(R3), .regOut(B));
  ProgramCounter programcounter_1 (.clk(clk), .rst(rst), .pc(programcounter_1_pc));
  Hex_Digit_Display hex_digit_display_16 (.value(R3[3:0]));  // open: dp
  RAM #(.addrWidth(6), .asyncread("true"), .trigger("falling")) ram_1 (
    .addr(programcounter_1_pc), .we(1'b0), .oe(1'b1), .clk(clk), .dout(ram_1_dout));  // open: din
  Register InstructionRegister (.D(ram_1_dout), .en(1'b1), .clk(clk), .Q(InstructionRegister_q), .clr(rst));
  IRDecoder irdecoder_1 (.IR(InstructionRegister_q), .clk(clk), .rst(rst), .sub(op), .Rd(Rd), .Rs(Rs));

  // Notes on the sheet:
  //   4c41 5341 7b43 537d
  //   b3 43 e2 32 82
endmodule

module IRDecoder (
  input  [7:0] IR,
  input  clk,
  input  rst,
  output sub,
  output [1:0] Rd,
  output [1:0] Rs
);

  wire and_1_out, not_1_out, not_2_out;

  not not_1 (not_1_out, IR[3]);
  not not_2 (not_2_out, IR[2]);
  and and_1 (and_1_out, not_1_out, not_2_out, IR[1], IR[0]);
  Register #(.width(2)) register_1 (.D(IR[7:6]), .en(1'b1), .clk(clk), .Q(Rd), .clr(rst));
  Register #(.width(2)) register_2 (.D(IR[5:4]), .en(1'b1), .clk(clk), .Q(Rs), .clr(rst));
  D_Flip_Flop d_ff_1 (.D(and_1_out), .clk(clk), .Q(sub), .reset(rst));  // open: Qn, preset
endmodule

module First4Instructions (
  input  rst
);

  wire clk, d_ff_1_q, FF, ld, ldi, op, or_1_out, ovrfl, register_1_q, regwe_1_reg0we, regwe_1_reg1we,
       regwe_1_reg2we, regwe_1_reg3we;
  wire [1:0] Rd, Rs;
  wire [5:0] programcounter_1_pc;
  wire [7:0] InstructionRegister_q, ram_2_dout;
  wire [15:0] A, B, bit_extender_1_out, multiplexer_1_out, multiplexer_2_out, R0, R1, R2, R3, ramOut,
       sixteenbitas2_1_sum;

  D_Flip_Flop d_ff_1 (.D(1'b1), .clk(clk), .Q(d_ff_1_q), .reset(rst));  // open: Qn, preset
  Clock u_clk (.out(clk));
  D_Flip_Flop d_ff_2 (.D(d_ff_1_q), .clk(clk), .Q(FF), .reset(rst));  // open: Qn, preset
  RAM #(.addrWidth(16), .asyncread("true"), .dataWidth(16), .trigger("falling")) ram_1 (
    .addr(B), .we(1'b0), .oe(1'b1), .clk(clk), .dout(ramOut));  // open: din
  Register #(.width(1)) register_1 (.D(FF), .en(ovrfl), .clk(clk), .Q(register_1_q), .clr(rst));
  SixteenBitAS2 sixteenbitas2_1 (.OP(op), .B(B), .A(A), .sum(sixteenbitas2_1_sum), .overflow(ovrfl));
  Hex_Digit_Display hex_digit_display_1 (.value(R0[15:12]));  // open: dp
  Hex_Digit_Display hex_digit_display_2 (.value(R0[11:8]));  // open: dp
  LED led_1 (.in(register_1_q));
  regWE regwe_1 (
    .Rd(Rd), .regWrite(FF), .reg0WE(regwe_1_reg0we), .reg1WE(regwe_1_reg1we), .reg2WE(regwe_1_reg2we),
    .reg3WE(regwe_1_reg3we));
  Hex_Digit_Display hex_digit_display_3 (.value(R0[7:4]));  // open: dp
  Hex_Digit_Display hex_digit_display_4 (.value(R0[3:0]));  // open: dp
  assign bit_extender_1_out = {{14{1'b0}}, Rs};  // Bit_Extender bit_extender_1
  Multiplexer #(.width(16)) multiplexer_1 (.in0(ramOut), .in1(bit_extender_1_out), .out(multiplexer_1_out), .sel(ldi));
  or or_1 (or_1_out, ldi, ld);
  Hex_Digit_Display hex_digit_display_5 (.value(R1[15:12]));  // open: dp
  Hex_Digit_Display hex_digit_display_6 (.value(R1[11:8]));  // open: dp
  Multiplexer #(.width(16)) multiplexer_2 (
    .in0(sixteenbitas2_1_sum), .in1(multiplexer_1_out), .out(multiplexer_2_out), .sel(or_1_out));
  Hex_Digit_Display hex_digit_display_7 (.value(R1[7:4]));  // open: dp
  Hex_Digit_Display hex_digit_display_8 (.value(R1[3:0]));  // open: dp
  Register #(.width(16)) u_R0 (.D(multiplexer_2_out), .en(regwe_1_reg0we), .clk(clk), .Q(R0), .clr(rst));
  Register #(.width(16)) u_R1 (.D(multiplexer_2_out), .en(regwe_1_reg1we), .clk(clk), .Q(R1), .clr(rst));
  Register #(.width(16)) u_R2 (.D(multiplexer_2_out), .en(regwe_1_reg2we), .clk(clk), .Q(R2), .clr(rst));
  Register #(.width(16)) u_R3 (.D(multiplexer_2_out), .en(regwe_1_reg3we), .clk(clk), .Q(R3), .clr(rst));
  Hex_Digit_Display hex_digit_display_9 (.value(R2[15:12]));  // open: dp
  Hex_Digit_Display hex_digit_display_10 (.value(R2[11:8]));  // open: dp
  Hex_Digit_Display hex_digit_display_11 (.value(R2[7:4]));  // open: dp
  Hex_Digit_Display hex_digit_display_12 (.value(R2[3:0]));  // open: dp
  Hex_Digit_Display hex_digit_display_13 (.value(R3[15:12]));  // open: dp
  Hex_Digit_Display hex_digit_display_14 (.value(R3[11:8]));  // open: dp
  Hex_Digit_Display hex_digit_display_15 (.value(R3[7:4]));  // open: dp
  scrSel scrsel_1 (.sel(Rd), .reg0(R0), .reg1(R1), .reg2(R2), .reg3(R3), .regOut(A));
  scrSel scrsel_2 (.sel(Rs), .reg0(R0), .reg1(R1), .reg2(R2), .reg3(R3), .regOut(B));
  ProgramCounter programcounter_1 (.clk(clk), .rst(rst), .pc(programcounter_1_pc));
  Hex_Digit_Display hex_digit_display_16 (.value(R3[3:0]));  // open: dp
  RAM #(.addrWidth(6), .asyncread("true"), .trigger("falling")) ram_2 (
    .addr(programcounter_1_pc), .we(1'b0), .oe(1'b1), .clk(clk), .dout(ram_2_dout));  // open: din
  Register InstructionRegister (.D(ram_2_dout), .en(1'b1), .clk(clk), .Q(InstructionRegister_q), .clr(rst));
  IRDecoder2 irdecoder2_1 (
    .IR(InstructionRegister_q), .clk(clk), .rst(rst), .ldi(ldi), .ld(ld), .sub(op), .Rd(Rd), .Rs(Rs));

  // Notes on the sheet:
  //   4c41 5341 7b43 537d
  //   b3 43 e2 32 82
endmodule

module IRDecoder2 (
  input  [7:0] IR,
  input  clk,
  input  rst,
  output ldi,
  output ld,
  output sub,
  output [1:0] Rd,
  output [1:0] Rs
);

  wire and_1_out, and_2_out, and_3_out, not_1_out, not_2_out, not_3_out;

  not not_1 (not_1_out, IR[3]);
  not not_2 (not_2_out, IR[2]);
  and and_1 (and_1_out, not_1_out, not_2_out, IR[1], IR[0]);
  and and_2 (and_2_out, IR[3], IR[2], IR[1], IR[0]);
  Register #(.width(2)) register_1 (.D(IR[7:6]), .en(1'b1), .clk(clk), .Q(Rd), .clr(rst));
  Register #(.width(2)) register_2 (.D(IR[5:4]), .en(1'b1), .clk(clk), .Q(Rs), .clr(rst));
  and and_3 (and_3_out, IR[3], IR[2], IR[1], not_3_out);
  D_Flip_Flop d_ff_1 (.D(and_1_out), .clk(clk), .Q(sub), .reset(rst));  // open: Qn, preset
  not not_3 (not_3_out, IR[0]);
  D_Flip_Flop d_ff_2 (.D(and_3_out), .clk(clk), .Q(ldi), .reset(rst));  // open: Qn, preset
  D_Flip_Flop d_ff_3 (.D(and_2_out), .clk(clk), .Q(ld), .reset(rst));  // open: Qn, preset
endmodule

module Fibonaccis (
  input  rst
);

  wire clk, d_ff_1_q, FF, ld, ldi, multiplexer_1_out, mv, op, or_1_out, ovrfl, register_1_q, regwe_1_reg0we,
       regwe_1_reg1we, regwe_1_reg2we, regwe_1_reg3we, st;
  wire [1:0] Rd, Rs;
  wire [5:0] programcounter_1_pc;
  wire [7:0] InstructionRegister_q, ram_2_dout;
  wire [15:0] A, B, bit_extender_1_out, multiplexer_2_out, multiplexer_3_out, multiplexer_4_out, R0, R1, R2,
       R3, ramOut, sixteenbitas2_1_sum;

  D_Flip_Flop d_ff_1 (.D(1'b1), .clk(clk), .Q(d_ff_1_q), .reset(rst));  // open: Qn, preset
  Clock u_clk (.out(clk));
  D_Flip_Flop d_ff_2 (.D(d_ff_1_q), .clk(clk), .Q(FF), .reset(rst));  // open: Qn, preset
  RAM #(.addrWidth(16), .asyncread("true"), .dataWidth(16), .trigger("falling")) ram_1 (
    .addr(B), .we(st), .oe(ld), .clk(clk), .din(A), .dout(ramOut));
  Multiplexer multiplexer_1 (.in0(FF), .in1(1'b0), .out(multiplexer_1_out), .sel(st));
  Register #(.width(1)) register_1 (.D(FF), .en(ovrfl), .clk(clk), .Q(register_1_q), .clr(rst));
  SixteenBitAS2 sixteenbitas2_1 (.OP(op), .B(B), .A(A), .sum(sixteenbitas2_1_sum), .overflow(ovrfl));
  Hex_Digit_Display hex_digit_display_1 (.value(R0[15:12]));  // open: dp
  Hex_Digit_Display hex_digit_display_2 (.value(R0[11:8]));  // open: dp
  LED led_1 (.in(register_1_q));
  Hex_Digit_Display hex_digit_display_3 (.value(R0[7:4]));  // open: dp
  Hex_Digit_Display hex_digit_display_4 (.value(R0[3:0]));  // open: dp
  assign bit_extender_1_out = {{14{1'b0}}, Rs};  // Bit_Extender bit_extender_1
  regWE regwe_1 (
    .Rd(Rd), .regWrite(multiplexer_1_out), .reg0WE(regwe_1_reg0we), .reg1WE(regwe_1_reg1we),
    .reg2WE(regwe_1_reg2we), .reg3WE(regwe_1_reg3we));
  Multiplexer #(.width(16)) multiplexer_2 (.in0(ramOut), .in1(bit_extender_1_out), .out(multiplexer_2_out), .sel(ldi));
  or or_1 (or_1_out, ldi, ld);
  Hex_Digit_Display hex_digit_display_5 (.value(R1[15:12]));  // open: dp
  Hex_Digit_Display hex_digit_display_6 (.value(R1[11:8]));  // open: dp
  Multiplexer #(.width(16)) multiplexer_3 (
    .in0(sixteenbitas2_1_sum), .in1(multiplexer_2_out), .out(multiplexer_3_out), .sel(or_1_out));
  Multiplexer #(.width(16)) multiplexer_4 (.in0(multiplexer_3_out), .in1(B), .out(multiplexer_4_out), .sel(mv));
  Hex_Digit_Display hex_digit_display_7 (.value(R1[7:4]));  // open: dp
  Hex_Digit_Display hex_digit_display_8 (.value(R1[3:0]));  // open: dp
  Register #(.width(16)) u_R0 (.D(multiplexer_4_out), .en(regwe_1_reg0we), .clk(clk), .Q(R0), .clr(rst));
  Register #(.width(16)) u_R1 (.D(multiplexer_4_out), .en(regwe_1_reg1we), .clk(clk), .Q(R1), .clr(rst));
  Register #(.width(16)) u_R2 (.D(multiplexer_4_out), .en(regwe_1_reg2we), .clk(clk), .Q(R2), .clr(rst));
  Register #(.width(16)) u_R3 (.D(multiplexer_4_out), .en(regwe_1_reg3we), .clk(clk), .Q(R3), .clr(rst));
  Hex_Digit_Display hex_digit_display_9 (.value(R2[15:12]));  // open: dp
  Hex_Digit_Display hex_digit_display_10 (.value(R2[11:8]));  // open: dp
  Hex_Digit_Display hex_digit_display_11 (.value(R2[7:4]));  // open: dp
  Hex_Digit_Display hex_digit_display_12 (.value(R2[3:0]));  // open: dp
  Hex_Digit_Display hex_digit_display_13 (.value(R3[15:12]));  // open: dp
  Hex_Digit_Display hex_digit_display_14 (.value(R3[11:8]));  // open: dp
  Hex_Digit_Display hex_digit_display_15 (.value(R3[7:4]));  // open: dp
  scrSel scrsel_1 (.sel(Rd), .reg0(R0), .reg1(R1), .reg2(R2), .reg3(R3), .regOut(A));
  scrSel scrsel_2 (.sel(Rs), .reg0(R0), .reg1(R1), .reg2(R2), .reg3(R3), .regOut(B));
  ProgramCounter programcounter_1 (.clk(clk), .rst(rst), .pc(programcounter_1_pc));
  Hex_Digit_Display hex_digit_display_16 (.value(R3[3:0]));  // open: dp
  RAM #(.addrWidth(6), .asyncread("true"), .trigger("falling")) ram_2 (
    .addr(programcounter_1_pc), .we(1'b0), .oe(1'b1), .clk(clk), .dout(ram_2_dout));  // open: din
  Register InstructionRegister (.D(ram_2_dout), .en(1'b1), .clk(clk), .Q(InstructionRegister_q), .clr(rst));
  IRDecoder3 irdecoder3_1 (
    .IR(InstructionRegister_q), .clk(clk), .rst(rst), .mv(mv), .st(st), .ldi(ldi), .ld(ld), .sub(op),
    .Rd(Rd), .Rs(Rs));

  // Notes on the sheet:
  //   4c41 5341 7b43 537d
  //   b3 43 e2 32 82
endmodule

module IRDecoder3 (
  input  [7:0] IR,
  input  clk,
  input  rst,
  output mv,
  output st,
  output ldi,
  output ld,
  output sub,
  output [1:0] Rd,
  output [1:0] Rs
);

  wire and_1_out, and_2_out, and_3_out, and_4_out, and_5_out, not_1_out, not_2_out, not_3_out, not_4_out,
       not_5_out, not_6_out;

  not not_1 (not_1_out, IR[3]);
  not not_2 (not_2_out, IR[2]);
  and and_1 (and_1_out, not_1_out, not_2_out, IR[1], IR[0]);
  and and_2 (and_2_out, IR[3], IR[2], IR[1], IR[0]);
  Register #(.width(2)) register_1 (.D(IR[7:6]), .en(1'b1), .clk(clk), .Q(Rd), .clr(rst));
  Register #(.width(2)) register_2 (.D(IR[5:4]), .en(1'b1), .clk(clk), .Q(Rs), .clr(rst));
  and and_3 (and_3_out, IR[3], IR[2], IR[1], not_3_out);
  D_Flip_Flop d_ff_1 (.D(and_1_out), .clk(clk), .Q(sub), .reset(rst));  // open: Qn, preset
  not not_3 (not_3_out, IR[0]);
  not not_4 (not_4_out, IR[3]);
  D_Flip_Flop d_ff_2 (.D(and_3_out), .clk(clk), .Q(ldi), .reset(rst));  // open: Qn, preset
  D_Flip_Flop d_ff_3 (.D(and_2_out), .clk(clk), .Q(ld), .reset(rst));  // open: Qn, preset
  not not_5 (not_5_out, IR[0]);
  and and_4 (and_4_out, not_4_out, IR[2], IR[1], not_5_out);
  D_Flip_Flop d_ff_4 (.D(and_4_out), .clk(clk), .Q(mv), .reset(rst));  // open: Qn, preset
  not not_6 (not_6_out, IR[2]);
  and and_5 (and_5_out, IR[3], not_6_out, IR[1], IR[0]);
  D_Flip_Flop d_ff_5 (.D(and_5_out), .clk(clk), .Q(st), .reset(rst));  // open: Qn, preset
endmodule

module Jump (
  input  rst,
  output [5:0] out_2
);

  wire clk, d_ff_1_q, FF, halt, jmp, ld, ldi, multiplexer_1_out, multiplexer_2_out, mv, op, or_1_out, ovrfl,
       register_1_q, regwe_1_reg0we, regwe_1_reg1we, regwe_1_reg2we, regwe_1_reg3we, st;
  wire [1:0] Rd, Rs;
  wire [5:0] programcounter2_1_pc, targ;
  wire [7:0] InstructionRegister_q, ram_2_dout;
  wire [15:0] A, B, bit_extender_1_out, multiplexer_3_out, multiplexer_4_out, multiplexer_5_out, R0, R1, R2,
       R3, ramOut, sixteenbitas2_1_sum;

  D_Flip_Flop d_ff_1 (.D(1'b1), .clk(clk), .Q(d_ff_1_q), .reset(rst));  // open: Qn, preset
  Clock u_clk (.out(clk));
  D_Flip_Flop d_ff_2 (.D(d_ff_1_q), .clk(clk), .Q(FF), .reset(rst));  // open: Qn, preset
  RAM #(.addrWidth(16), .asyncread("true"), .dataWidth(16), .trigger("falling")) ram_1 (
    .addr(B), .we(st), .oe(ld), .clk(clk), .din(A), .dout(ramOut));
  Multiplexer multiplexer_1 (.in0(FF), .in1(1'b0), .out(multiplexer_1_out), .sel(st));
  Multiplexer multiplexer_2 (.in0(multiplexer_1_out), .in1(1'b0), .out(multiplexer_2_out), .sel(jmp));
  Register #(.width(1)) register_1 (.D(FF), .en(ovrfl), .clk(clk), .Q(register_1_q), .clr(rst));
  SixteenBitAS2 sixteenbitas2_1 (.OP(op), .B(B), .A(A), .sum(sixteenbitas2_1_sum), .overflow(ovrfl));
  Hex_Digit_Display hex_digit_display_1 (.value(R0[15:12]));  // open: dp
  Hex_Digit_Display hex_digit_display_2 (.value(R0[11:8]));  // open: dp
  LED led_1 (.in(register_1_q));
  Hex_Digit_Display hex_digit_display_3 (.value(R0[7:4]));  // open: dp
  Hex_Digit_Display hex_digit_display_4 (.value(R0[3:0]));  // open: dp
  assign bit_extender_1_out = {{14{1'b0}}, Rs};  // Bit_Extender bit_extender_1
  regWE regwe_1 (
    .Rd(Rd), .regWrite(multiplexer_2_out), .reg0WE(regwe_1_reg0we), .reg1WE(regwe_1_reg1we),
    .reg2WE(regwe_1_reg2we), .reg3WE(regwe_1_reg3we));
  Multiplexer #(.width(16)) multiplexer_3 (.in0(ramOut), .in1(bit_extender_1_out), .out(multiplexer_3_out), .sel(ldi));
  or or_1 (or_1_out, ldi, ld);
  Hex_Digit_Display hex_digit_display_5 (.value(R1[15:12]));  // open: dp
  Hex_Digit_Display hex_digit_display_6 (.value(R1[11:8]));  // open: dp
  Multiplexer #(.width(16)) multiplexer_4 (
    .in0(sixteenbitas2_1_sum), .in1(multiplexer_3_out), .out(multiplexer_4_out), .sel(or_1_out));
  Multiplexer #(.width(16)) multiplexer_5 (.in0(multiplexer_4_out), .in1(B), .out(multiplexer_5_out), .sel(mv));
  Hex_Digit_Display hex_digit_display_7 (.value(R1[7:4]));  // open: dp
  Hex_Digit_Display hex_digit_display_8 (.value(R1[3:0]));  // open: dp
  Register #(.width(16)) u_R0 (.D(multiplexer_5_out), .en(regwe_1_reg0we), .clk(clk), .Q(R0), .clr(rst));
  Register #(.width(16)) u_R1 (.D(multiplexer_5_out), .en(regwe_1_reg1we), .clk(clk), .Q(R1), .clr(rst));
  Register #(.width(16)) u_R2 (.D(multiplexer_5_out), .en(regwe_1_reg2we), .clk(clk), .Q(R2), .clr(rst));
  Register #(.width(16)) u_R3 (.D(multiplexer_5_out), .en(regwe_1_reg3we), .clk(clk), .Q(R3), .clr(rst));
  Hex_Digit_Display hex_digit_display_9 (.value(R2[15:12]));  // open: dp
  Hex_Digit_Display hex_digit_display_10 (.value(R2[11:8]));  // open: dp
  Hex_Digit_Display hex_digit_display_11 (.value(R2[7:4]));  // open: dp
  Hex_Digit_Display hex_digit_display_12 (.value(R2[3:0]));  // open: dp
  Hex_Digit_Display hex_digit_display_13 (.value(R3[15:12]));  // open: dp
  Hex_Digit_Display hex_digit_display_14 (.value(R3[11:8]));  // open: dp
  Hex_Digit_Display hex_digit_display_15 (.value(R3[7:4]));  // open: dp
  scrSel scrsel_1 (.sel(Rd), .reg0(R0), .reg1(R1), .reg2(R2), .reg3(R3), .regOut(A));
  scrSel scrsel_2 (.sel(Rs), .reg0(R0), .reg1(R1), .reg2(R2), .reg3(R3), .regOut(B));
  ProgramCounter2 programcounter2_1 (.targ(targ), .jmp(jmp), .clk(clk), .rst(rst), .pc(programcounter2_1_pc));
  cyclecounter cyclecounter_1 (.halt(halt), .clk(clk), .rst(rst), .cycles(out_2));
  Hex_Digit_Display hex_digit_display_16 (.value(R3[3:0]));  // open: dp
  RAM #(.addrWidth(6), .asyncread("true"), .trigger("falling")) ram_2 (
    .addr(programcounter2_1_pc), .we(1'b0), .oe(1'b1), .clk(clk), .dout(ram_2_dout));  // open: din
  Register InstructionRegister (.D(ram_2_dout), .en(1'b1), .clk(clk), .Q(InstructionRegister_q), .clr(rst));
  IRDecoder4 irdecoder4_1 (
    .IR(InstructionRegister_q), .clk(clk), .rst(rst), .mv(mv), .st(st), .ldi(ldi), .ld(ld), .sub(op),
    .Rd(Rd), .Rs(Rs), .jmp(jmp), .targ(targ), .halt(halt));

  // Notes on the sheet:
  //   4c41 5341 7b43 537d
  //   b3 43 e2 32 82
endmodule

module IRDecoder4 (
  input  [7:0] IR,
  input  clk,
  input  rst,
  output mv,
  output st,
  output ldi,
  output ld,
  output sub,
  output [1:0] Rd,
  output [1:0] Rs,
  output jmp,
  output [5:0] targ,
  output halt
);

  wire and_1_out, and_2_out, and_3_out, and_4_out, and_5_out, and_6_out, and_7_out, and_9_out, and_10_out,
       d_ff_2_q, halt_t, not_1_out, not_2_out, not_3_out, not_4_out, not_5_out, not_6_out, not_7_out,
       not_8_out;

  not not_1 (not_1_out, IR[3]);
  not not_2 (not_2_out, IR[2]);
  and and_1 (and_1_out, not_1_out, not_2_out, IR[1], IR[0]);
  not not_3 (not_3_out, IR[1]);
  and and_2 (and_2_out, IR[3], IR[2], IR[1], IR[0]);
  Register #(.width(2)) register_1 (.D(IR[7:6]), .en(1'b1), .clk(clk), .Q(Rd), .clr(rst));
  Register #(.width(2)) register_2 (.D(IR[5:4]), .en(1'b1), .clk(clk), .Q(Rs), .clr(rst));
  not not_4 (not_4_out, IR[0]);
  and and_3 (and_3_out, not_3_out, not_4_out);
  and and_4 (and_4_out, IR[4], IR[5]);
  and and_5 (and_5_out, IR[6], IR[7]);
  and and_6 (and_6_out, IR[3], IR[2], IR[1], not_5_out);
  D_Flip_Flop d_ff_1 (.D(and_1_out), .clk(clk), .Q(sub), .reset(rst));  // open: Qn, preset
  D_Flip_Flop d_ff_2 (.D(1'b1), .clk(clk), .Q(d_ff_2_q), .reset(rst));  // open: Qn, preset
  Register #(.width(6)) register_3 (.D(IR[7:2]), .en(1'b1), .clk(clk), .Q(targ), .clr(rst));
  not not_5 (not_5_out, IR[0]);
  not not_6 (not_6_out, IR[3]);
  D_Flip_Flop d_ff_3 (.D(and_6_out), .clk(clk), .Q(ldi), .reset(rst));  // open: Qn, preset
  D_Flip_Flop d_ff_4 (.D(and_2_out), .clk(clk), .Q(ld), .reset(rst));  // open: Qn, preset
  D_Flip_Flop d_ff_5 (.D(and_7_out), .clk(clk), .Q(halt), .reset(rst));  // open: Qn, preset
  and and_7 (and_7_out, and_4_out, halt_t, and_5_out);
  not not_7 (not_7_out, IR[0]);
  and and_8 (halt_t, not_6_out, IR[2], IR[1], not_7_out);
  D_Flip_Flop d_ff_6 (.D(halt_t), .clk(clk), .Q(mv), .reset(rst));  // open: Qn, preset
  and and_9 (and_9_out, d_ff_2_q, and_3_out);
  not not_8 (not_8_out, IR[2]);
  and and_10 (and_10_out, IR[3], not_8_out, IR[1], IR[0]);
  D_Flip_Flop d_ff_7 (.D(and_10_out), .clk(clk), .Q(st), .reset(rst));  // open: Qn, preset
  D_Flip_Flop d_ff_8 (.D(and_9_out), .clk(clk), .Q(jmp), .reset(rst));  // open: Qn, preset
endmodule

module ProgramCounter2 (
  input  [5:0] targ,
  input  jmp,
  input  clk,
  input  rst,
  output [5:0] pc
);

  wire [5:0] adder_1_out, multiplexer_1_out;

  Multiplexer #(.width(6)) multiplexer_1 (.in0(adder_1_out), .in1(targ), .out(multiplexer_1_out), .sel(jmp));
  Register #(.width(6)) R (.D(multiplexer_1_out), .en(1'b1), .clk(clk), .Q(pc), .clr(rst));
  Adder #(.width(6)) adder_1 (.a(6'b000001), .b(pc), .out(adder_1_out));  // open: cin, cout
endmodule

module cyclecounter (
  input  halt,
  input  clk,
  input  rst,
  output [5:0] cycles
);

  wire not_1_out, register_1_q;
  wire [5:0] adder_1_out;

  Register #(.width(1)) register_1 (.D(1'b1), .en(halt), .clk(clk), .Q(register_1_q), .clr(rst));
  not not_1 (not_1_out, register_1_q);
  Register #(.width(6)) R (.D(adder_1_out), .en(not_1_out), .clk(clk), .Q(cycles), .clr(rst));
  Adder #(.width(6)) adder_1 (.a(6'b000001), .b(cycles), .out(adder_1_out));  // open: cin, cout
endmodule

module ImprovedJump (
  input  rst,
  output [5:0] out_2
);

  wire clk, d_ff_1_q, FF, halt, jmp, ld, ldi, multiplexer_1_out, multiplexer_2_out, mv, op, or_1_out, ovrfl,
       register_1_q, regwe_1_reg0we, regwe_1_reg1we, regwe_1_reg2we, regwe_1_reg3we, st;
  wire [1:0] Rd, Rs;
  wire [5:0] programcounter2_1_pc, targ;
  wire [7:0] InstructionRegister_q, ram_2_dout;
  wire [15:0] A, B, bit_extender_1_out, multiplexer_3_out, multiplexer_4_out, multiplexer_5_out, R0, R1, R2,
       R3, ramOut, sixteenbitas2_1_sum;

  D_Flip_Flop d_ff_1 (.D(1'b1), .clk(clk), .Q(d_ff_1_q), .reset(rst));  // open: Qn, preset
  Clock u_clk (.out(clk));
  D_Flip_Flop d_ff_2 (.D(d_ff_1_q), .clk(clk), .Q(FF), .reset(rst));  // open: Qn, preset
  RAM #(.addrWidth(16), .asyncread("true"), .dataWidth(16), .trigger("falling")) ram_1 (
    .addr(B), .we(st), .oe(ld), .clk(clk), .din(A), .dout(ramOut));
  Multiplexer multiplexer_1 (.in0(FF), .in1(1'b0), .out(multiplexer_1_out), .sel(st));
  Multiplexer multiplexer_2 (.in0(multiplexer_1_out), .in1(1'b0), .out(multiplexer_2_out), .sel(jmp));
  Register #(.width(1)) register_1 (.D(FF), .en(ovrfl), .clk(clk), .Q(register_1_q), .clr(rst));
  SixteenBitAS2 sixteenbitas2_1 (.OP(op), .B(B), .A(A), .sum(sixteenbitas2_1_sum), .overflow(ovrfl));
  Hex_Digit_Display hex_digit_display_1 (.value(R0[15:12]));  // open: dp
  Hex_Digit_Display hex_digit_display_2 (.value(R0[11:8]));  // open: dp
  LED led_1 (.in(register_1_q));
  Hex_Digit_Display hex_digit_display_3 (.value(R0[7:4]));  // open: dp
  Hex_Digit_Display hex_digit_display_4 (.value(R0[3:0]));  // open: dp
  assign bit_extender_1_out = {{14{1'b0}}, Rs};  // Bit_Extender bit_extender_1
  regWE regwe_1 (
    .Rd(Rd), .regWrite(multiplexer_2_out), .reg0WE(regwe_1_reg0we), .reg1WE(regwe_1_reg1we),
    .reg2WE(regwe_1_reg2we), .reg3WE(regwe_1_reg3we));
  Multiplexer #(.width(16)) multiplexer_3 (.in0(ramOut), .in1(bit_extender_1_out), .out(multiplexer_3_out), .sel(ldi));
  or or_1 (or_1_out, ldi, ld);
  Hex_Digit_Display hex_digit_display_5 (.value(R1[15:12]));  // open: dp
  Hex_Digit_Display hex_digit_display_6 (.value(R1[11:8]));  // open: dp
  Multiplexer #(.width(16)) multiplexer_4 (
    .in0(sixteenbitas2_1_sum), .in1(multiplexer_3_out), .out(multiplexer_4_out), .sel(or_1_out));
  Multiplexer #(.width(16)) multiplexer_5 (.in0(multiplexer_4_out), .in1(B), .out(multiplexer_5_out), .sel(mv));
  Hex_Digit_Display hex_digit_display_7 (.value(R1[7:4]));  // open: dp
  Hex_Digit_Display hex_digit_display_8 (.value(R1[3:0]));  // open: dp
  Register #(.width(16)) u_R0 (.D(multiplexer_5_out), .en(regwe_1_reg0we), .clk(clk), .Q(R0), .clr(rst));
  Register #(.width(16)) u_R1 (.D(multiplexer_5_out), .en(regwe_1_reg1we), .clk(clk), .Q(R1), .clr(rst));
  Register #(.width(16)) u_R2 (.D(multiplexer_5_out), .en(regwe_1_reg2we), .clk(clk), .Q(R2), .clr(rst));
  Register #(.width(16)) u_R3 (.D(multiplexer_5_out), .en(regwe_1_reg3we), .clk(clk), .Q(R3), .clr(rst));
  Hex_Digit_Display hex_digit_display_9 (.value(R2[15:12]));  // open: dp
  Hex_Digit_Display hex_digit_display_10 (.value(R2[11:8]));  // open: dp
  Hex_Digit_Display hex_digit_display_11 (.value(R2[7:4]));  // open: dp
  Hex_Digit_Display hex_digit_display_12 (.value(R2[3:0]));  // open: dp
  Hex_Digit_Display hex_digit_display_13 (.value(R3[15:12]));  // open: dp
  Hex_Digit_Display hex_digit_display_14 (.value(R3[11:8]));  // open: dp
  Hex_Digit_Display hex_digit_display_15 (.value(R3[7:4]));  // open: dp
  scrSel scrsel_1 (.sel(Rd), .reg0(R0), .reg1(R1), .reg2(R2), .reg3(R3), .regOut(A));
  scrSel scrsel_2 (.sel(Rs), .reg0(R0), .reg1(R1), .reg2(R2), .reg3(R3), .regOut(B));
  ProgramCounter2 programcounter2_1 (.targ(targ), .jmp(jmp), .clk(clk), .rst(rst), .pc(programcounter2_1_pc));
  cyclecounter cyclecounter_1 (.halt(halt), .clk(clk), .rst(rst), .cycles(out_2));
  Hex_Digit_Display hex_digit_display_16 (.value(R3[3:0]));  // open: dp
  RAM #(.addrWidth(6), .asyncread("true"), .trigger("falling")) ram_2 (
    .addr(programcounter2_1_pc), .we(1'b0), .oe(1'b1), .clk(clk), .dout(ram_2_dout));  // open: din
  Register InstructionRegister (.D(ram_2_dout), .en(1'b1), .clk(clk), .Q(InstructionRegister_q), .clr(rst));
  IRDecoder4 irdecoder4_1 (
    .IR(InstructionRegister_q), .clk(clk), .rst(rst), .mv(mv), .st(st), .ldi(ldi), .ld(ld), .sub(op),
    .Rd(Rd), .Rs(Rs), .jmp(jmp), .targ(targ), .halt(halt));

  // Notes on the sheet:
  //   4c41 5341 7b43 537d
  //   b3 43 e2 32 82
endmodule

module IRDecoder5 (
  input  [7:0] IR,
  input  clk,
  input  rst,
  output mv,
  output st,
  output ldi,
  output ld,
  output sub,
  output [1:0] Rd,
  output [1:0] Rs,
  output jmp,
  output [5:0] targ,
  output halt
);

  wire and_1_out, and_2_out, and_3_out, and_4_out, and_5_out, and_6_out, and_7_out, and_10_out, d_ff_2_q,
       halt_t, not_1_out, not_2_out, not_3_out, not_4_out, not_5_out, not_6_out, not_7_out, not_8_out;

  not not_1 (not_1_out, IR[3]);
  not not_2 (not_2_out, IR[2]);
  and and_1 (and_1_out, not_1_out, not_2_out, IR[1], IR[0]);
  not not_3 (not_3_out, IR[1]);
  and and_2 (and_2_out, IR[3], IR[2], IR[1], IR[0]);
  Register #(.width(2)) register_1 (.D(IR[7:6]), .en(1'b1), .clk(clk), .Q(Rd), .clr(rst));
  Register #(.width(2)) register_2 (.D(IR[5:4]), .en(1'b1), .clk(clk), .Q(Rs), .clr(rst));
  not not_4 (not_4_out, IR[0]);
  and and_3 (and_3_out, not_3_out, not_4_out);
  and and_4 (and_4_out, IR[4], IR[5]);
  and and_5 (and_5_out, IR[6], IR[7]);
  and and_6 (and_6_out, IR[3], IR[2], IR[1], not_5_out);
  D_Flip_Flop d_ff_1 (.D(and_1_out), .clk(clk), .Q(sub), .reset(rst));  // open: Qn, preset
  D_Flip_Flop d_ff_2 (.D(1'b1), .clk(clk), .Q(d_ff_2_q), .reset(rst));  // open: Qn, preset
  Multiplexer #(.width(6)) multiplexer_1 (.in0(IR[7:2]), .in1({6{1'b0}}), .out(targ), .sel(rst));
  not not_5 (not_5_out, IR[0]);
  not not_6 (not_6_out, IR[3]);
  D_Flip_Flop d_ff_3 (.D(and_6_out), .clk(clk), .Q(ldi), .reset(rst));  // open: Qn, preset
  D_Flip_Flop d_ff_4 (.D(and_2_out), .clk(clk), .Q(ld), .reset(rst));  // open: Qn, preset
  D_Flip_Flop d_ff_5 (.D(and_7_out), .clk(clk), .Q(halt), .reset(rst));  // open: Qn, preset
  and and_7 (and_7_out, and_4_out, halt_t, and_5_out);
  not not_7 (not_7_out, IR[0]);
  and and_8 (halt_t, not_6_out, IR[2], IR[1], not_7_out);
  D_Flip_Flop d_ff_6 (.D(halt_t), .clk(clk), .Q(mv), .reset(rst));  // open: Qn, preset
  and and_9 (jmp, d_ff_2_q, and_3_out);
  not not_8 (not_8_out, IR[2]);
  and and_10 (and_10_out, IR[3], not_8_out, IR[1], IR[0]);
  D_Flip_Flop d_ff_7 (.D(and_10_out), .clk(clk), .Q(st), .reset(rst));  // open: Qn, preset
endmodule
